# Fritzing sketch Fritzing-Board-NodeMCU-Final Send (saved by Fritzing 0.9.4)
breadboards: 1

parts:
  U1 = ESP8266 WiFi Module [part_number=ESP8266]  # not connected
  U1_2 = NodeMCU V1.0
  LED1 = smd LED [color="Red (633nm)" package="1206 [SMD]"]
  R1 = Resistor [tolerance=±5% resistance=220 package=THT]
  DHT11_1 = DHT11 module

nets:
  N1: U1_2.D1, R1.Pin_0
  N2: U1_2.D4, DHT11_1.DATA
  3V3: U1_2.3V3, DHT11_1.VCC
  GND: U1_2.GND, LED1.anode, DHT11_1.GND
  N3: LED1.cathode, R1.Pin_1

custom parts:
  NodeMCU V1.0: ESP9266 based NodeMCU
  DHT11 module: https://cdn-learn.adafruit.com/downloads/pdf/dht.pdf DHT11 black pcb module reference by:https://github.com/adafruit/Fritzing-Library/blob/master/parts/DHT11%20Humitidy%20and%20Temperature%20Sensor.fzpz
